# Fritzing sketch ampop (saved by Fritzing 0.6.5b)
breadboards: 1

parts:
  U1 = LM 358 Dual Op-Amp [package="DIP8 [THT]"]
  R1 = Resistor [tolerance=±5% resistance=10k package=THT]
  R3 = Resistor [tolerance=±5% resistance=10k package=THT]
  R7 = Resistor [tolerance=±5% resistance=100 package=THT]
  R8 = Resistor [tolerance=±5% resistance=10k package=THT]
  R9 = Resistor [tolerance=±5% resistance=68k package=THT]
  MIC1 = Microphone
  C1 = Electrolytic Capacitor [capacitance=10μF package="100 mil [THT, electrolytic]"]
  J1 = female pin header, 6 pins [form="♀ (female)"]
  Composants1 = JeeNode wireless microcontroller

nets:
  N1: U1.connector0, R1.Pin_1, R9.Pin_0
  N2: U1.connector1, R7.Pin_0, R9.Pin_1
  N3: U1.connector2, R3.Pin_0, C1.-
  GND: U1.connector3, R3.Pin_1, R7.Pin_1, MIC1.pin1, J1.pin4, Composants1.GND
  5V: U1.connector7, J1.pin6, Composants1.PWR
  N4: R1.Pin_0, J1.pin2, Composants1.A0
  N5: R8.Pin_0, MIC1.pin2, C1.+
  3.3V: R8.Pin_1, J1.pin3, Composants1.VCC

notes:
  Electret&ampliop test setup
  MonitoringIsNotEvil
